// Logisim project 8 bit Register.circ as structural Verilog: 2 circuits, main circuit main
module main (
  input  pass_through,
  input  Load,
  input  Enable,
  input  D1,
  input  D2,
  input  D3,
  input  D4,
  input  D5,
  input  D6,
  input  D7,
  input  D8,
  output out_12,
  output out_13,
  output out_14,
  output out_15,
  output out_16,
  output out_17,
  output out_18,
  output out_19
);

  wire and_1_out, and_2_out, and_3_out, and_4_out, and_5_out, and_6_out, and_7_out, and_8_out, and_9_out,
       and_10_out, and_11_out, and_12_out, and_13_out, and_14_out, and_15_out, and_16_out, and_17_out,
       clock_1_out, D1_q, D1_qn, D2_q, D2_qn, D3_q, D3_qn, D4_q, D4_qn, D5_q, D5_qn, D6_q, D6_qn, D7_q,
       D7_qn, D8_q, D8_qn, not_1_out, not_2_out, not_3_out, not_4_out, not_5_out, not_6_out, not_7_out,
       not_8_out, not_9_out, not_10_out, not_11_out, not_12_out, not_13_out, not_14_out, not_15_out,
       not_16_out, not_17_out, not_18_out, or_1_out, or_2_out, or_3_out, or_4_out, or_5_out, or_6_out,
       or_7_out, or_8_out;

  Clock clock_1 (.out(clock_1_out));
  not not_1 (not_1_out, pass_through);
  not not_2 (not_2_out, pass_through);
  not not_3 (not_3_out, Load);
  not not_4 (not_4_out, Load);
  not not_5 (not_5_out, Load);
  not not_6 (not_6_out, Load);
  not not_7 (not_7_out, Load);
  not not_8 (not_8_out, Load);
  not not_9 (not_9_out, Load);
  not not_10 (not_10_out, Load);
  and and_1 (and_1_out, not_1_out, not_2_out);
  and and_2 (and_2_out, D1_q, not_3_out);
  and and_3 (and_3_out, Load, D1);
  and and_4 (and_4_out, D2_q, not_4_out);
  and and_5 (and_5_out, Load, D2);
  and and_6 (and_6_out, D3_q, not_5_out);
  and and_7 (and_7_out, Load, D3);
  and and_8 (and_8_out, D4_q, not_6_out);
  and and_9 (and_9_out, Load, D4);
  and and_10 (and_10_out, D5_q, not_7_out);
  and and_11 (and_11_out, Load, D5);
  and and_12 (and_12_out, D6_q, not_8_out);
  and and_13 (and_13_out, Load, D6);
  and and_14 (and_14_out, D7_q, not_9_out);
  and and_15 (and_15_out, Load, D7);
  and and_16 (and_16_out, D8_q, not_10_out);
  and and_17 (and_17_out, Load, D8);
  or or_1 (or_1_out, and_2_out, and_3_out);
  or or_2 (or_2_out, and_4_out, and_5_out);
  or or_3 (or_3_out, and_6_out, and_7_out);
  or or_4 (or_4_out, and_8_out, and_9_out);
  or or_5 (or_5_out, and_10_out, and_11_out);
  or or_6 (or_6_out, and_12_out, and_13_out);
  or or_7 (or_7_out, and_14_out, and_15_out);
  or or_8 (or_8_out, and_16_out, and_17_out);
  D_Flip_Flop u_D1 (.clk(clock_1_out), .D(or_1_out), .Q(D1_q), .Qn(D1_qn), .en(Enable));  // open: preset, reset
  not not_11 (not_11_out, D1_qn);
  D_Flip_Flop u_D2 (.clk(clock_1_out), .D(or_2_out), .Q(D2_q), .Qn(D2_qn), .en(Enable));  // open: preset, reset
  not not_12 (not_12_out, D2_qn);
  D_Flip_Flop u_D3 (.clk(clock_1_out), .D(or_3_out), .Q(D3_q), .Qn(D3_qn), .en(Enable));  // open: preset, reset
  not not_13 (not_13_out, D3_qn);
  D_Flip_Flop u_D4 (.clk(clock_1_out), .D(or_4_out), .Q(D4_q), .Qn(D4_qn), .en(Enable));  // open: preset, reset
  not not_14 (not_14_out, D4_qn);
  D_Flip_Flop u_D5 (.clk(clock_1_out), .D(or_5_out), .Q(D5_q), .Qn(D5_qn), .en(Enable));  // open: preset, reset
  not not_15 (not_15_out, D5_qn);
  D_Flip_Flop u_D6 (.clk(clock_1_out), .D(or_6_out), .Q(D6_q), .Qn(D6_qn), .en(Enable));  // open: preset, reset
  not not_16 (not_16_out, D6_qn);
  D_Flip_Flop u_D7 (.clk(clock_1_out), .D(or_7_out), .Q(D7_q), .Qn(D7_qn), .en(Enable));  // open: preset, reset
  not not_17 (not_17_out, D7_qn);
  D_Flip_Flop u_D8 (.clk(clock_1_out), .D(or_8_out), .Q(D8_q), .Qn(D8_qn), .en(Enable));  // open: preset, reset
  not not_18 (not_18_out, D8_qn);
  assign out_12 = and_1_out ? not_11_out : 1'bz;  // Controlled_Buffer controlled_buffer_1
  assign out_13 = and_1_out ? not_12_out : 1'bz;  // Controlled_Buffer controlled_buffer_2
  assign out_14 = and_1_out ? not_13_out : 1'bz;  // Controlled_Buffer controlled_buffer_3
  assign out_15 = and_1_out ? not_14_out : 1'bz;  // Controlled_Buffer controlled_buffer_4
  assign out_16 = and_1_out ? not_15_out : 1'bz;  // Controlled_Buffer controlled_buffer_5
  assign out_17 = and_1_out ? not_16_out : 1'bz;  // Controlled_Buffer controlled_buffer_6
  assign out_18 = and_1_out ? not_17_out : 1'bz;  // Controlled_Buffer controlled_buffer_7
  assign out_19 = and_1_out ? not_18_out : 1'bz;  // Controlled_Buffer controlled_buffer_8
  LED led_1 (.in(D1_q));
  LED led_2 (.in(D2_q));
  LED led_3 (.in(D3_q));
  LED led_4 (.in(D4_q));
  LED led_5 (.in(D5_q));
  LED led_6 (.in(D6_q));
  LED led_7 (.in(D7_q));
  LED led_8 (.in(D8_q));
endmodule

module _1_Bit_Reg (
  input  pass_through,
  input  Load,
  input  Enable,
  input  D1,
  output out_5
);

  wire and_1_out, and_2_out, and_3_out, clock_1_out, D1_q, D1_qn, not_1_out, not_2_out, not_3_out, not_4_out,
       or_1_out;

  Clock clock_1 (.out(clock_1_out));
  not not_1 (not_1_out, pass_through);
  not not_2 (not_2_out, pass_through);
  not not_3 (not_3_out, Load);
  and and_1 (and_1_out, not_1_out, not_2_out);
  and and_2 (and_2_out, D1_q, not_3_out);
  and and_3 (and_3_out, Load, D1);
  or or_1 (or_1_out, and_2_out, and_3_out);
  D_Flip_Flop u_D1 (.clk(clock_1_out), .D(or_1_out), .Q(D1_q), .Qn(D1_qn), .en(Enable));  // open: preset, reset
  not not_4 (not_4_out, D1_qn);
  assign out_5 = and_1_out ? not_4_out : 1'bz;  // Controlled_Buffer controlled_buffer_1
  LED led_1 (.in(D1_q));
endmodule
