// Logisim project Adder_Circuits.circ as structural Verilog: 6 circuits, main circuit Half Adder
module Half_Adder (
  input  A,
  input  B,
  output Sum,
  output Cout
);

  xor xor_1 (Sum, A, B);
  and and_1 (Cout, A, B);
endmodule

module Full_Adder (
  input  A,
  input  B,
  input  Cin,
  output Sum,
  output Cout
);

  wire half_adder_1_cout, half_adder_1_sum, half_adder_2_cout;

  Half_Adder half_adder_1 (.A(A), .B(B), .Sum(half_adder_1_sum), .Cout(half_adder_1_cout));
  Half_Adder half_adder_2 (.A(half_adder_1_sum), .B(Cin), .Sum(Sum), .Cout(half_adder_2_cout));
  or or_1 (Cout, half_adder_1_cout, half_adder_2_cout);
endmodule

module Parallel_Adder (
  input  B3,
  input  A3,
  input  B2,
  input  A2,
  input  B1,
  input  A1,
  input  B0,
  input  A0,
  output Sum,
  output COut,
  output Sum_2,
  output Sum_3,
  output Sum_4
);

  wire full_adder_2_cout, full_adder_3_cout, full_adder_4_cout;

  Full_Adder full_adder_1 (.A(A3), .B(B3), .Cin(full_adder_2_cout), .Sum(Sum), .Cout(COut));
  Full_Adder full_adder_2 (.A(A2), .B(B2), .Cin(full_adder_3_cout), .Sum(Sum_2), .Cout(full_adder_2_cout));
  Full_Adder full_adder_3 (.A(A1), .B(B1), .Cin(full_adder_4_cout), .Sum(Sum_3), .Cout(full_adder_3_cout));
  Full_Adder full_adder_4 (.A(A0), .B(B0), .Cin(1'b0), .Sum(Sum_4), .Cout(full_adder_4_cout));

  // Notes on the sheet:
  //   MSB
  //   Carry In
  //   FA3
  //   Carry In
  //   FA2
  //   Carry Out
  //   FA1
  //   Carry In
  //   Carry Out
  //   LSB
  //   Carry In
  //   FA0
  //   Carry Out
endmodule

module Look_Ahead_Carry (
  input  B3,
  input  A3,
  input  B2,
  input  A2,
  input  B1,
  input  A1,
  input  B0,
  input  A0,
  input  Cin0,
  output C_out4,
  output Sum4,
  output Sum3,
  output Sum2,
  output Sum1
);

  wire and_1_out, and_2_out, and_3_out, and_4_out, and_5_out, and_6_out, and_7_out, and_8_out, and_9_out,
       and_10_out, and_11_out, and_12_out, and_13_out, and_14_out, or_2_out, or_3_out, or_4_out, or_5_out,
       or_6_out, or_7_out, or_8_out;

  or or_1 (C_out4, and_5_out, and_1_out, and_2_out, and_3_out, and_4_out);
  and and_1 (and_1_out, or_2_out, and_9_out);
  and and_2 (and_2_out, or_2_out, or_4_out, and_12_out);
  and and_3 (and_3_out, or_2_out, or_4_out, or_6_out, and_14_out);
  and and_4 (and_4_out, or_2_out, or_4_out, or_6_out, or_8_out, Cin0);
  and and_5 (and_5_out, B3, A3);
  or or_2 (or_2_out, B3, A3);
  Full_Adder full_adder_1 (.A(A3), .B(B3), .Cin(or_3_out), .Sum(Sum4));  // open: Cout
  or or_3 (or_3_out, and_9_out, and_6_out, and_7_out, and_8_out);
  and and_6 (and_6_out, or_4_out, and_12_out);
  and and_7 (and_7_out, or_4_out, or_6_out, and_14_out);
  and and_8 (and_8_out, or_4_out, or_6_out, or_8_out, Cin0);
  and and_9 (and_9_out, B2, A2);
  or or_4 (or_4_out, B2, A2);
  Full_Adder full_adder_2 (.A(A2), .B(B2), .Cin(or_5_out), .Sum(Sum3));  // open: Cout
  or or_5 (or_5_out, and_12_out, and_10_out, and_11_out);
  and and_10 (and_10_out, or_6_out, and_14_out);
  and and_11 (and_11_out, or_6_out, or_8_out, Cin0);
  and and_12 (and_12_out, B1, A1);
  or or_6 (or_6_out, B1, A1);
  Full_Adder full_adder_3 (.A(A1), .B(B1), .Cin(or_7_out), .Sum(Sum2));  // open: Cout
  or or_7 (or_7_out, and_14_out, and_13_out);
  and and_13 (and_13_out, or_8_out, Cin0);
  and and_14 (and_14_out, B0, A0);
  or or_8 (or_8_out, B0, A0);
  Full_Adder full_adder_4 (.A(A0), .B(B0), .Cin(Cin0), .Sum(Sum1));  // open: Cout

  // Notes on the sheet:
  //   FA3
  //   MSB
  //   FA2
  //   FA1
  //   FA0
  //   LSB
endmodule

module _4_Bit_Adder (
);

  Look_Ahead_Carry look_ahead_carry_1 ();  // open: Cin0, B3, A3, B2, A2, B1, A1, B0, A0, C_out4, Sum4, Sum3, Sum2, Sum1

  // Notes on the sheet:
  //   4 Bit Adder
endmodule

module _8_Bit_Adder (
);

  _4_Bit_Adder u_4_bit_adder_1 ();
  _4_Bit_Adder u_4_bit_adder_2 ();
endmodule
