// Logisim project Counter_Circuits.circ as structural Verilog: 4 circuits, main circuit Counter
module Counter (
  output [3:0] out_1
);

  wire and_1_out, and_2_out, button_1_out;

  Button button_1 (.out(button_1_out));
  J_K_Flip_Flop j_k_ff_1 (.J(1'b1), .clk(button_1_out), .K(1'b1), .Q(out_1[3]));  // open: Qn, preset, en, reset
  J_K_Flip_Flop j_k_ff_2 (.J(out_1[3]), .clk(button_1_out), .K(out_1[3]), .Q(out_1[3]));  // open: Qn, preset, en, reset
  and and_1 (and_1_out, out_1[3], out_1[3]);
  J_K_Flip_Flop j_k_ff_3 (
    .J(and_1_out), .clk(button_1_out), .K(and_1_out), .Q(out_1[1]));  // open: Qn, preset, en, reset
  and and_2 (and_2_out, out_1[3], out_1[3], out_1[1]);
  J_K_Flip_Flop j_k_ff_4 (
    .J(and_2_out), .clk(button_1_out), .K(and_2_out), .Q(out_1[0]));  // open: Qn, preset, en, reset
  Hex_Digit_Display hex_digit_display_1 (.value({{2{out_1[3]}}, out_1[1:0]}));  // open: dp

  assign out_1[2] = out_1[3];
endmodule

module _4_Bit_Counter_out (
  output [3:0] out_1
);

  wire and_1_out, and_2_out, button_1_out;

  Button button_1 (.out(button_1_out));
  J_K_Flip_Flop j_k_ff_1 (.J(1'b1), .clk(button_1_out), .K(1'b1), .Q(out_1[3]));  // open: Qn, preset, en, reset
  J_K_Flip_Flop j_k_ff_2 (.J(out_1[3]), .clk(button_1_out), .K(out_1[3]), .Q(out_1[2]));  // open: Qn, preset, en, reset
  and and_1 (and_1_out, out_1[3], out_1[2]);
  J_K_Flip_Flop j_k_ff_3 (
    .J(and_1_out), .clk(button_1_out), .K(and_1_out), .Q(out_1[1]));  // open: Qn, preset, en, reset
  and and_2 (and_2_out, out_1[3], out_1[2], out_1[1]);
  J_K_Flip_Flop j_k_ff_4 (
    .J(and_2_out), .clk(button_1_out), .K(and_2_out), .Q(out_1[0]));  // open: Qn, preset, en, reset
endmodule

module _4_bit_Counter (
  output [3:0] out_1
);

  wire and_1_out, and_2_out, button_1_out;

  Button button_1 (.out(button_1_out));
  J_K_Flip_Flop j_k_ff_1 (.J(1'b1), .clk(button_1_out), .K(1'b1), .Q(out_1[3]));  // open: Qn, preset, en, reset
  J_K_Flip_Flop j_k_ff_2 (.J(out_1[3]), .clk(button_1_out), .K(out_1[3]), .Q(out_1[3]));  // open: Qn, preset, en, reset
  and and_1 (and_1_out, out_1[3], out_1[3]);
  J_K_Flip_Flop j_k_ff_3 (
    .J(and_1_out), .clk(button_1_out), .K(and_1_out), .Q(out_1[1]));  // open: Qn, preset, en, reset
  and and_2 (and_2_out, out_1[3], out_1[3], out_1[1]);
  J_K_Flip_Flop j_k_ff_4 (
    .J(and_2_out), .clk(button_1_out), .K(and_2_out), .Q(out_1[0]));  // open: Qn, preset, en, reset
  Hex_Digit_Display hex_digit_display_1 (.value({{2{out_1[3]}}, out_1[1:0]}));  // open: dp

  assign out_1[2] = out_1[3];
endmodule

module _2_Bit_Counter (
  output [1:0] out_1
);

  wire button_1_out;

  Button button_1 (.out(button_1_out));
  J_K_Flip_Flop j_k_ff_1 (.J(1'b1), .clk(button_1_out), .K(1'b1), .Q(out_1[1]));  // open: Qn, preset, en, reset
  J_K_Flip_Flop j_k_ff_2 (.J(out_1[1]), .clk(button_1_out), .K(out_1[1]), .Q(out_1[0]));  // open: Qn, preset, en, reset
endmodule
