// Logisim project Decoders_Circuits.circ as structural Verilog
module BCD_to_Dec (
  input  A0,
  input  A1,
  input  A2,
  input  A3,
  output Dec0,
  output Dec1,
  output Dec2,
  output Dec3,
  output Dec4,
  output Dec5,
  output Dec6,
  output Dec7,
  output Dec8,
  output Dec9
);

  wire not_1_out, not_2_out, not_3_out, not_4_out, not_5_out, not_6_out, not_7_out, not_8_out, not_9_out,
       not_10_out, not_11_out, not_12_out, not_13_out, not_14_out, not_15_out, not_16_out, not_17_out,
       not_18_out, not_19_out, not_20_out, not_21_out, not_22_out, not_23_out, not_24_out, not_25_out;

  not not_1 (not_1_out, A0);
  not not_2 (not_2_out, A1);
  not not_3 (not_3_out, A2);
  not not_4 (not_4_out, A3);
  not not_5 (not_5_out, A1);
  not not_6 (not_6_out, A2);
  not not_7 (not_7_out, A3);
  and and_1 (Dec0, not_1_out, not_2_out, not_3_out, not_4_out);
  and and_2 (Dec1, A0, not_5_out, not_6_out, not_7_out);
  not not_8 (not_8_out, A0);
  not not_9 (not_9_out, A2);
  not not_10 (not_10_out, A3);
  not not_11 (not_11_out, A2);
  not not_12 (not_12_out, A3);
  and and_3 (Dec2, not_8_out, A1, not_9_out, not_10_out);
  and and_4 (Dec3, A0, A1, not_11_out, not_12_out);
  not not_13 (not_13_out, A0);
  not not_14 (not_14_out, A1);
  not not_15 (not_15_out, A3);
  not not_16 (not_16_out, A1);
  not not_17 (not_17_out, A3);
  and and_5 (Dec4, not_13_out, not_14_out, A2, not_15_out);
  and and_6 (Dec5, A0, not_16_out, A2, not_17_out);
  not not_18 (not_18_out, A0);
  not not_19 (not_19_out, A3);
  and and_7 (Dec6, not_18_out, A1, A2, not_19_out);
  and and_8 (Dec7, A0, A1, A2, not_20_out);
  not not_20 (not_20_out, A3);
  not not_21 (not_21_out, A0);
  not not_22 (not_22_out, A1);
  not not_23 (not_23_out, A2);
  and and_9 (Dec8, not_21_out, not_22_out, not_23_out, A3);
  not not_24 (not_24_out, A1);
  and and_10 (Dec9, A0, not_24_out, not_25_out, A3);
  not not_25 (not_25_out, A2);

  // Notes on the sheet:
  //   LSB
  //   MSB
  //   BCD/Dec Decoder
endmodule

module Bin_to_7_Seg (
);

  _7_Segment_Display u_7_segment_display_1 ();  // open: g, f, a, b, e, d, c, dp
endmodule
