// Logisim project Encoder_Circuits.circ as structural Verilog
module Dec_BCD_Encoder (
  input  Dec1,
  input  Dec2,
  input  Dec3,
  input  Dec4,
  input  Dec5,
  input  Dec6,
  input  Dec7,
  input  Dec8,
  input  Dec9,
  output _0,
  output A0,
  output A1,
  output A2,
  output A3
);

  or or_1 (A0, Dec1, Dec3, Dec5, Dec7, Dec9);
  or or_2 (A1, Dec3, Dec2, Dec6, Dec7);
  or or_3 (A2, Dec4, Dec5, Dec6, Dec7);
  or or_4 (A3, Dec8, Dec9);

  assign _0 = 1'b0;

  // Notes on the sheet:
  //   Dec0
  //   Dec/BCD Encoder
  //   Binary
endmodule

module Dec_to_Bin_Encoder (
  input  Dec1,
  input  Dec2,
  input  Dec3,
  input  Dec4,
  input  Dec5,
  input  Dec6,
  input  Dec7,
  input  Dec8,
  input  Dec9,
  output A0,
  output A1,
  output A2,
  output A3
);

  Dec_BCD_Encoder dec_bcd_encoder_1 (
    .Dec1(Dec1), .Dec2(Dec2), .Dec3(Dec3), .Dec4(Dec4), .Dec5(Dec5), .Dec6(Dec6), .Dec7(Dec7), .Dec8(Dec8),
    .Dec9(Dec9), .A0(A0), .A1(A1), .A2(A2), .A3(A3));  // open: _0

  // Notes on the sheet:
  //   Dec/BCD Encoder
  //   LSB
  //   MSB
endmodule
