// Logisim project Latch_Circuits.circ as structural Verilog
module SR_Latch_Active_High (
  output Q,
  output Not_Q
);

  wire R_out, S_out;

  Button R (.out(R_out));
  Button S (.out(S_out));
  nor nor_1 (Q, R_out, Not_Q);
  nor nor_2 (Not_Q, Q, S_out);
endmodule

module SR_Latch_Active_Low (
  input  nS,
  input  nR,
  output Q,
  output nQ
);

  nand nand_1 (Q, nS, nQ);
  nand nand_2 (nQ, Q, nR);
endmodule

module Gated_SR_Latch (
  input  Enable,
  output Q,
  output Not_Q
);

  wire and_1_out, and_2_out, R_out, S_out;

  Button R (.out(R_out));
  Button S (.out(S_out));
  and and_1 (and_1_out, R_out, Enable);
  and and_2 (and_2_out, Enable, S_out);
  nor nor_1 (Q, and_1_out, Not_Q);
  nor nor_2 (Not_Q, Q, and_2_out);
endmodule

module Gated_D_Latch (
  input  Enable,
  input  Data,
  output Q,
  output Not_Q
);

  wire and_1_out, and_2_out, not_1_out;

  not not_1 (not_1_out, Data);
  and and_1 (and_1_out, not_1_out, Enable);
  and and_2 (and_2_out, Enable, Data);
  nor nor_1 (Q, and_1_out, Not_Q);
  nor nor_2 (Not_Q, Q, and_2_out);
endmodule

module Edge_Trigger (
  input  Trigger,
  output CLK
);

  wire nand_1_out, not_1_out, not_2_out, not_3_out;

  not not_1 (not_1_out, Trigger);
  Pull_Resistor pull_resistor_1 (.node(Trigger));
  not not_2 (not_2_out, not_1_out);
  not not_3 (not_3_out, not_2_out);
  nand nand_1 (nand_1_out, not_3_out, Trigger);
  not not_4 (CLK, nand_1_out);
endmodule

module D_FlipFlop (
  input  En,
  input  Data,
  output Q,
  output Not_Q
);

  wire and_1_out, Clock_out, edge_trigger_1_clk;

  Clock Clock (.out(Clock_out));
  Edge_Trigger edge_trigger_1 (.Trigger(Clock_out), .CLK(edge_trigger_1_clk));
  and and_1 (and_1_out, edge_trigger_1_clk, En);
  Gated_D_Latch gated_d_latch_1 (.Enable(and_1_out), .Data(Data), .Q(Q), .Not_Q(Not_Q));

  // Notes on the sheet:
  //   Trigger
  //   D FlipFlop
endmodule

module JK_FlipFlop (
  input  J,
  input  Trigger,
  input  K,
  output Q,
  output Not_Q
);

  wire and_1_out, and_2_out, nand_1_out, not_1_out, not_2_out;

  not not_1 (not_1_out, Trigger);
  not not_2 (not_2_out, nand_1_out);
  nand nand_1 (nand_1_out, not_1_out, Trigger);
  and and_1 (and_1_out, J, not_2_out);
  and and_2 (and_2_out, not_2_out, K);
  nor nor_1 (Q, and_1_out, Not_Q);
  nor nor_2 (Not_Q, Q, and_2_out);
endmodule
