// Logisim project 1_Bit_ALU.circ as structural Verilog: 3 circuits, main circuit 1 Bit ALU
module _1_Bit_ALU (
  input  [2:0] Operation,
  input  SUB_nADD,
  input  Cin,
  input  A,
  input  B,
  input  Less,
  output Result,
  output Cout,
  output Set
);

  wire and_1_out, nor_1_out, or_1_out, xor_1_out, xor_2_out;

  xor xor_1 (xor_1_out, SUB_nADD, B);
  and and_1 (and_1_out, A, B);
  or or_1 (or_1_out, A, B);
  xor xor_2 (xor_2_out, A, B);
  nor nor_1 (nor_1_out, A, B);
  Adder #(.width(1)) adder_1 (.a(A), .b(xor_1_out), .out(Set), .cin(Cin), .cout(Cout));
  Multiplexer #(.select(3), .enable("false")) multiplexer_1 (
    .in0(and_1_out), .in1(or_1_out), .in2(xor_2_out), .in3(nor_1_out), .in4(Set), .in5(Less), .out(Result),
    .sel(Operation));  // open: in6, in7

  // Notes on the sheet:
  //   ALU Operations
  //   000 AND
  //   001 OR
  //   010 XOR
  //   011 NOR
  //   100 ADD/SUB
  //   101 LESS
endmodule

module _8_Bit_ALU (
  input  [7:0] A,
  input  [2:0] Op,
  input  SUB,
  input  [7:0] B,
  output [7:0] Result,
  output Zero_Flag
);

  wire n1_bit_alu_1_cout, n1_bit_alu_2_cout, n1_bit_alu_3_cout, n1_bit_alu_4_cout, n1_bit_alu_5_cout,
       n1_bit_alu_6_cout, n1_bit_alu_7_cout, n1_bit_alu_8_set;

  _1_Bit_ALU u_1_bit_alu_1 (
    .A(A[0]), .B(B[0]), .Less(n1_bit_alu_8_set), .Result(Result[0]), .SUB_nADD(SUB), .Cin(SUB),
    .Operation(Op), .Cout(n1_bit_alu_1_cout));  // open: Set
  _1_Bit_ALU u_1_bit_alu_2 (
    .A(A[1]), .B(B[1]), .Less(1'b0), .Result(Result[1]), .SUB_nADD(SUB), .Cin(n1_bit_alu_1_cout),
    .Operation(Op), .Cout(n1_bit_alu_2_cout));  // open: Set
  _1_Bit_ALU u_1_bit_alu_3 (
    .A(A[2]), .B(B[2]), .Less(1'b0), .Result(Result[2]), .SUB_nADD(SUB), .Cin(n1_bit_alu_2_cout),
    .Operation(Op), .Cout(n1_bit_alu_3_cout));  // open: Set
  _1_Bit_ALU u_1_bit_alu_4 (
    .A(A[3]), .B(B[3]), .Less(1'b0), .Result(Result[3]), .SUB_nADD(SUB), .Cin(n1_bit_alu_3_cout),
    .Operation(Op), .Cout(n1_bit_alu_4_cout));  // open: Set
  _1_Bit_ALU u_1_bit_alu_5 (
    .A(A[4]), .B(B[4]), .Less(1'b0), .Result(Result[4]), .SUB_nADD(SUB), .Cin(n1_bit_alu_4_cout),
    .Operation(Op), .Cout(n1_bit_alu_5_cout));  // open: Set
  _1_Bit_ALU u_1_bit_alu_6 (
    .A(A[5]), .B(B[5]), .Less(1'b0), .Result(Result[5]), .SUB_nADD(SUB), .Cin(n1_bit_alu_5_cout),
    .Operation(Op), .Cout(n1_bit_alu_6_cout));  // open: Set
  _1_Bit_ALU u_1_bit_alu_7 (
    .A(A[6]), .B(B[6]), .Less(1'b0), .Result(Result[6]), .SUB_nADD(SUB), .Cin(n1_bit_alu_6_cout),
    .Operation(Op), .Cout(n1_bit_alu_7_cout));  // open: Set
  _1_Bit_ALU u_1_bit_alu_8 (
    .A(A[7]), .B(B[7]), .Result(Result[7]), .SUB_nADD(SUB), .Cin(n1_bit_alu_7_cout), .Operation(Op),
    .Set(n1_bit_alu_8_set));  // open: Less, Cout
  nor nor_1 (Zero_Flag, Result[0], Result[1], Result[2], Result[3], Result[4], Result[5], Result[6], Result[7]);

  // Notes on the sheet:
  //   ALU Operations
  //   000 AND
  //   001 OR
  //   010 XOR
  //   011 NOR
  //   100 ADD/SUB
  //   101 LESS
endmodule

module ALU (
  input  SUB,
  input  [2:0] Op,
  input  [7:0] A,
  input  [7:0] B,
  output [7:0] Result,
  output Zero_Flag
);

  _8_Bit_ALU u_8_bit_alu_1 (.A(A), .B(B), .Result(Result), .Zero_Flag(Zero_Flag), .SUB(SUB), .Op(Op));

  // Notes on the sheet:
  //   ALU Operations
  //   000 AND
  //   001 OR
  //   010 XOR
  //   011 NOR
  //   100 ADD/SUB
  //   101 LESS
endmodule
