// Logisim project Comparator_Circuits - Copy.circ as structural Verilog
module Comparator (
  input  A,
  input  B,
  output A_B,
  output A_B_2,
  output A_B_3
);

  wire not_1_out, not_2_out;

  not not_1 (not_1_out, B);
  not not_2 (not_2_out, A);
  and u_A_B (A_B, A, not_1_out);
  nor u_A_B_2 (A_B_2, A_B, A_B_3);
  and u_A_B_3 (A_B_3, B, not_2_out);
endmodule

module _4_Bit_Comparator (
  input  A0,
  input  B0,
  input  A1,
  input  B1,
  input  A2,
  input  B2,
  input  A_B_in,
  input  A3,
  input  B3,
  input  A_B_in_2,
  input  A_B_in_3,
  output A_B,
  output A_B_2,
  output A_B_3
);

  wire and_1_out, and_2_out, and_3_out, and_5_out, and_6_out, and_7_out, comparator_1_a_b,
       comparator_1_a_b_2, comparator_1_a_b_3, comparator_2_a_b, comparator_2_a_b_2, comparator_2_a_b_3,
       comparator_3_a_b, comparator_3_a_b_2, comparator_3_a_b_3, comparator_4_a_b, comparator_4_a_b_2,
       comparator_4_a_b_3;

  Comparator comparator_1 (
    .A(A0), .B(B0), .A_B(comparator_1_a_b), .A_B_2(comparator_1_a_b_2), .A_B_3(comparator_1_a_b_3));
  Comparator comparator_2 (
    .A(A1), .B(B1), .A_B(comparator_2_a_b), .A_B_2(comparator_2_a_b_2), .A_B_3(comparator_2_a_b_3));
  Comparator comparator_3 (
    .A(A2), .B(B2), .A_B(comparator_3_a_b), .A_B_2(comparator_3_a_b_2), .A_B_3(comparator_3_a_b_3));
  Comparator comparator_4 (
    .A(A3), .B(B3), .A_B(comparator_4_a_b), .A_B_2(comparator_4_a_b_2), .A_B_3(comparator_4_a_b_3));
  and and_1 (and_1_out, comparator_1_a_b_2, A_B_in, comparator_2_a_b);
  and and_2 (and_2_out, comparator_1_a_b_2, comparator_2_a_b_2, A_B_in, comparator_3_a_b);
  and and_3 (and_3_out, comparator_1_a_b_2, comparator_2_a_b_2, A_B_in, comparator_3_a_b_2, comparator_4_a_b);
  and and_4 (A_B_3, comparator_1_a_b_2, comparator_2_a_b_2, A_B_in_3, comparator_3_a_b_2, comparator_4_a_b_2);
  and and_5 (and_5_out, comparator_1_a_b_2, A_B_in_2, comparator_2_a_b_3);
  and and_6 (and_6_out, comparator_1_a_b_2, A_B_in_2, comparator_3_a_b_3);
  and and_7 (and_7_out, comparator_1_a_b_2, comparator_2_a_b_2, A_B_in_2, comparator_3_a_b_2, comparator_4_a_b_3);
  or or_1 (A_B, comparator_1_a_b, and_1_out, and_2_out, and_3_out);
  or or_2 (A_B_2, comparator_1_a_b_3, and_5_out, and_6_out, and_7_out);
endmodule

module _8_Bit_Comparator (
  input  B0,
  input  B1,
  input  B4,
  input  B2,
  input  B5,
  input  B3,
  input  B6,
  input  B7,
  input  A_B_in,
  input  A_B_in_2,
  input  A_B_in_3,
  input  A4,
  input  A5,
  input  A0,
  input  A6,
  input  A1,
  input  A7,
  input  A2,
  input  A3,
  output A_B,
  output A_B_2,
  output A_B_3
);

  wire n4_bit_comparator_1_a_b, n4_bit_comparator_1_a_b_2, n4_bit_comparator_1_a_b_3;

  _4_Bit_Comparator u_4_bit_comparator_1 (
    .A0(A0), .B0(B0), .A1(A1), .B1(B1), .A2(A2), .B2(B2), .A3(A3), .B3(B3), .A_B(n4_bit_comparator_1_a_b),
    .A_B_2(n4_bit_comparator_1_a_b_2), .A_B_3(n4_bit_comparator_1_a_b_3), .A_B_in_3(A_B_in_2),
    .A_B_in(A_B_in), .A_B_in_2(A_B_in_3));
  _4_Bit_Comparator u_4_bit_comparator_2 (
    .A0(A4), .B0(B4), .A1(A5), .B1(B5), .A2(A6), .B2(B6), .A3(A7), .B3(B7), .A_B(A_B), .A_B_2(A_B_3),
    .A_B_3(A_B_2), .A_B_in_3(n4_bit_comparator_1_a_b_3), .A_B_in(n4_bit_comparator_1_a_b),
    .A_B_in_2(n4_bit_comparator_1_a_b_2));

  // Notes on the sheet:
  //   LSB
  //   MSB
endmodule
