// Logisim project Demultiplexer_Circuit.circ as structural Verilog: 2 circuits, main circuit main
module main (
  input  S0,
  input  S1,
  input  Data,
  output D0,
  output D1,
  output D2,
  output D3
);

  wire not_1_out, not_2_out;

  not not_1 (not_1_out, S0);
  not not_2 (not_2_out, S1);
  and and_1 (D0, Data, not_2_out, not_1_out);
  and and_2 (D1, Data, not_2_out, S0);
  and and_3 (D2, S1, not_1_out);
  and and_4 (D3, Data, S1, S0);

  // Notes on the sheet:
  //   LSB
  //   MSB
endmodule

module DEMUX (
  input  S0,
  input  S1,
  input  Data_In,
  output D0,
  output D1,
  output D2,
  output D3
);

  main main_1 (.S0(S0), .S1(S1), .Data(Data_In), .D0(D0), .D1(D1), .D2(D2), .D3(D3));

  // Notes on the sheet:
  //   Data Select
  //   LSB
  //   MSB
  //   Data Output
endmodule
