// Logisim project OUTPUT.circ as structural Verilog: 1 circuit, main circuit main
module main (
);

  // _8_bit_Register_main main_1: pin names not known
  // ALU alu_1: pin names not known
endmodule
